// Logisim project LC-3-v2.circ as structural Verilog: 17 circuits, main circuit main
// RES
module main (
  input  Reset,
  output out_2,
  output out_3,
  output out_4,
  output out_5,
  output out_6,
  output out_7,
  output out_8,
  output [15:0] out_9,
  output [15:0] out_10,
  output [15:0] out_11,
  output [15:0] out_12,
  output [15:0] out_13,
  output [15:0] out_14,
  output [15:0] out_15,
  output [15:0] out_16,
  output [15:0] out_17,
  output halt,
  output [15:0] out_19,
  output [15:0] out_20,
  output [15:0] out_21,
  output [15:0] out_22
);

  wire decodeir_1_writereg, getcst_1_usecst, or16_1_out_2, or16_2_out_2, ramctrl_1_memload,
       ramctrl_1_memstore, regpc_1_write_r7, writer7_1_writereg_2;
  wire [2:0] nzp_1_nzp, writer7_1_dr_sr;
  wire [15:0] alu_1_output, getcst_1_cst, RegIN, registres_1_out_sr1, registres_1_out_sr2, writer7_1_regin;

  RegPC regpc_1 (
    .H(out_3), .PC(out_9), .Reset(Reset), .IR(out_10), .R(registres_1_out_sr1), .TestNZP(out_5),
    .Jump(out_4), .Write_R7(regpc_1_write_r7));
  BiClock biclock_1 (.reset(Reset), .signal0(out_2), .signal1(out_3));
  // Probe on out_9
  GetAddr getaddr_1 (.PC(out_9), .BaseR(registres_1_out_sr1), .IR(out_10), .Addr(out_11), .Fetch(out_2));
  // Probe on out_11
  // Probe on out_12
  // Probe on out_13
  RAM #(.addrWidth(16), .dataWidth(16), .bus("separate"), .Select("high"), .simpleMode("false")) ram_1 (
    .addr(out_11), .din(out_12), .data(out_13), .str(ramctrl_1_memstore), .clk(ramctrl_1_memstore),
    .ld(ramctrl_1_memload));  // open: sel, clr
  LED led_1 (.in(out_6));
  RamCtrl ramctrl_1 (
    .Store(out_7), .Fetch(out_2), .Exec(out_3), .Load(out_6), .MemStore(ramctrl_1_memstore),
    .MemLoad(ramctrl_1_memload));
  LED led_2 (.in(out_7));
  Register #(.width(16), .trigger("falling"), .Select("low")) RegIR (
    .D(out_13), .Q(out_10), .clk(out_2));  // open: en, clr
  DecodeIR decodeir_1 (.IR(out_10), .Jump(out_4), .WriteReg(decodeir_1_writereg), .Load(out_6), .Store(out_7));
  // Probe on writer7_1_dr_sr
  // Probe on out_10[8:6]
  // Probe on out_10[2:0]
  // Probe on getcst_1_cst
  GetCst getcst_1 (.IR(out_10), .Cst(getcst_1_cst), .UseCst(getcst_1_usecst));
  // Probe on out_10[15:14]
  and and_1 (out_8, decodeir_1_writereg, out_3);
  WriteR7 writer7_1 (
    .WriteReg(out_8), .PC(out_9), .WriteValOut(RegIN), .Exec(out_3), .WriteR7(regpc_1_write_r7),
    .DR(out_10[11:9]), .RegIn(writer7_1_regin), .WriteReg_2(writer7_1_writereg_2), .DR_SR(writer7_1_dr_sr));
  Registres registres_1 (
    .SR1(out_10[8:6]), .IN(writer7_1_regin), .SR2(out_10[2:0]), .WriteReg(writer7_1_writereg_2),
    .DR_SR(writer7_1_dr_sr), .OUT_SR1(registres_1_out_sr1), .OUT_SR2(registres_1_out_sr2), .OUT_SR(out_12),
    .R0(out_14), .R1(out_15), .R2(out_16), .R3(out_17), .R4(out_19), .R5(out_20), .R6(out_21), .R7(out_22));
  // Probe on registres_1_out_sr2
  // Probe on registres_1_out_sr1
  ALU alu_1 (
    .UseCst(getcst_1_usecst), .e2(out_10[15:14]), .Input1(registres_1_out_sr1), .Input2(registres_1_out_sr2),
    .Cst(getcst_1_cst), .Output(alu_1_output));
  Or16 or16_1 (.in_1(out_10), .out_2(or16_1_out_2));
  Or16 or16_2 (.in_1(out_9), .out_2(or16_2_out_2));
  // Probe on alu_1_output
  NZP nzp_1 (.RES(RegIN), .NZP(nzp_1_nzp), .IR(out_10), .TestNZP(out_5), .WriteReg(out_8));
  // Probe on nzp_1_nzp
  and and_2 (halt, ~or16_1_out_2, or16_2_out_2);  // AND_Gate
  // Probe on out_14
  // Probe on out_15
  // Probe on out_16
  // Probe on out_17
  // Probe on out_19
  // Probe on out_20
  // Probe on out_21
  // Probe on out_22
  WriteVal writeval_1 (.Load(out_6), .ALURes(alu_1_output), .MemOUT(out_13), .IR(out_10), .PC(out_9), .RegIN(RegIN));

  // Other names for the same wires on the sheet: Addr[15:0] = out_11; Condition = out_5; Exec = out_3; Fetch = out_2;
  //   IR[15:0] = out_10; JumpInstr = out_4; Load = out_6; MemIN[15:0] = out_12; MemOUT[15:0] = out_13;
  //   PC[15:0] = out_9; R0[15:0] = out_14; R1[15:0] = out_15; R2[15:0] = out_16; R3[15:0] = out_17; R4[15:0] = out_19;
  //   R5[15:0] = out_20; R6[15:0] = out_21; R7[15:0] = out_22; Store = out_7; WriteReg = out_8

  // Notes on the sheet:
  //   R
  //   IR
  //   R
  //   IR
  //   RAM
  //   Traces (NE PAS MODIFIER)______________________________________________________________________________________________________
  //   GetOp
  //   Arret des traces au 1er NOP
endmodule

module ALU (
  input  [15:0] Input1,
  input  [15:0] Input2,
  input  [15:0] Cst,
  input  UseCst,
  input  [1:0] e2,
  output [15:0] Output
);

  wire [15:0] adder_1_out, and_1_out, multiplexer_1_out, not_1_out, scan16_1_out_3;

  Multiplexer #(.width(16), .enable("false")) multiplexer_1 (
    .in0(Input2), .in1(Cst), .out(multiplexer_1_out), .sel(UseCst));
  Adder #(.width(16)) adder_1 (.a(multiplexer_1_out), .b(Input1), .out(adder_1_out));  // open: cin, cout
  assign and_1_out = Input1 & multiplexer_1_out;  // AND_Gate and_1, 16 bits wide
  Multiplexer #(.select(2), .width(16), .enable("false")) multiplexer_2 (
    .in0(adder_1_out), .in1(and_1_out), .in2(not_1_out), .in3(scan16_1_out_3), .out(Output), .sel(e2));
  assign not_1_out = ~Input1;  // NOT_Gate not_1, 16 bits wide
  SCAN16 scan16_1 (.in_1(multiplexer_1_out), .out_3(scan16_1_out_3), .in_2(Input1));
endmodule

module BiClock (
  input  reset,
  output signal0,
  output signal1
);

  wire and_1_out, horloge_out, not_1_out, register_1_q;

  Clock horloge (.out(horloge_out));
  not not_1 (not_1_out, register_1_q);
  Register #(.width(1), .trigger("falling"), .Select("low")) register_1 (
    .D(not_1_out), .Q(register_1_q), .clk(horloge_out), .clr(reset));  // open: en
  and and_1 (and_1_out, horloge_out, ~reset);  // AND_Gate
  and and_2 (signal0, ~register_1_q, and_1_out);  // AND_Gate
  and and_3 (signal1, register_1_q, and_1_out);

  // Notes on the sheet:
  //   Ce module divise une horloge en deux sous-horloges alternées
  //   Chronogrammes :
  //   horloge: 0101010101 signal0: 0100010001 signal1: 000100010
  //   registre 1-bit
  //   Enable
  //   select : 0 / 1
endmodule

module DecodeIR (
  input  [15:0] IR,
  output Jump,
  output Load,
  output Store,
  output WriteReg
);

  wire and_1_out;

  and and_1 (and_1_out, IR[12], ~IR[13]);  // AND_Gate
  and and_2 (Jump, ~IR[12], ~IR[13]);  // AND_Gate
  and and_3 (Load, ~IR[12], IR[13]);  // AND_Gate
  and and_4 (Store, IR[12], IR[13]);
  // Probe on and_1_out
  or or_1 (WriteReg, Load, and_1_out);

  // Notes on the sheet:
  //   Types d'instructions
  //   Si l'instruction est arithmétique ou bien un chargement
  //   Instruction modifiant les registres ?
endmodule

module GetAddr (
  input  [15:0] IR,
  input  Fetch,
  input  [15:0] PC,
  input  [15:0] BaseR,
  output [15:0] Addr
);

  wire or_1_out;
  wire [15:0] adder_1_out, adder_2_out, multiplexer_1_out, offset6_1_off6, offset9_1_off9;

  Offset9 offset9_1 (.IR(IR), .Off9(offset9_1_off9));
  Offset6 offset6_1 (.IR(IR), .Off6(offset6_1_off6));
  Adder #(.width(16)) adder_1 (.a(offset6_1_off6), .b(BaseR), .out(adder_1_out));  // open: cin, cout
  Adder #(.width(16)) adder_2 (.a(offset9_1_off9), .b(PC), .out(adder_2_out), .cin(1'b1));  // open: cout
  Multiplexer #(.width(16), .disabled(0), .enable("false")) multiplexer_1 (
    .in0(adder_2_out), .in1(adder_1_out), .out(multiplexer_1_out), .sel(IR[14]));
  or or_1 (or_1_out, ~IR[13], Fetch);  // OR_Gate
  Multiplexer #(.width(16), .disabled(0), .enable("false")) multiplexer_2 (
    .in0(multiplexer_1_out), .in1(PC), .out(Addr), .sel(or_1_out));

  // Notes on the sheet:
  //   PC+SEXT(Offset6)
  //   b14: label or BaseR?
  //   PC+SEXT(Offset9)
  //   b13: Load ou Store?
  //   Pourquoi ?
endmodule

module GetCst (
  input  [15:0] IR,
  output [15:0] Cst,
  output UseCst
);

  assign Cst = {{11{IR[4]}}, IR[4:0]};  // Bit_Extender bit_extender_1

  assign UseCst = IR[5];
endmodule

module NZP (
  input  [15:0] RES,
  input  WriteReg,
  input  [15:0] IR,
  output [2:0] NZP,
  output TestNZP
);

  wire and_3_out, and_4_out, and_5_out, and_6_out, or_1_out;
  wire [1:0] and_2_out;

  and and_1 (and_2_out[1], ~RES[0], ~RES[1], ~RES[2], ~RES[3], ~RES[4], ~RES[5], ~RES[6], ~RES[7], ~RES[8], ~RES[9], ~RES[10], ~RES[11], ~RES[12], ~RES[13], ~RES[14], ~RES[15]);  // AND_Gate
  and and_2 (and_2_out[0], ~RES[15], ~and_2_out[1]);  // AND_Gate
  and and_3 (and_3_out, NZP[0], IR[9]);
  and and_4 (and_4_out, NZP[1], IR[10]);
  and and_5 (and_5_out, NZP[2], IR[11]);
  Multiplexer #(.width(3), .enable("false")) multiplexer_1 (
    .in0(NZP), .in1({RES[15], and_2_out}), .out(NZP), .sel(WriteReg));
  or or_1 (or_1_out, and_3_out, and_4_out, and_5_out);
  and and_6 (and_6_out, ~IR[12], ~IR[13], ~IR[14], ~IR[15]);  // AND_Gate
  and and_7 (TestNZP, or_1_out, and_6_out);

  // Notes on the sheet:
  //   (Resultat du calcul courant)
  //   (Instruction courante)
  //   Si tous les bits sont à zéro -> Z
  //   Si le bit 15 vaut 1 -> N
  //   Si le registre != zéro et bit n°15 != 1 -> P
  //   Test flag P
  //   Test flag Z
  //   Test flag N
  //   Si l'instruction courante est BR
  //   Si WriteReg vaut 1: on met à jour NZP$Sinon on ne change pas la valeur
  //   Test de saut : vrai si au moins un flag est vrai
  //   Valeur actuelle du registre d'état NZP
endmodule

// Off6
module Offset6 (
  input  [15:0] IR,
  output [15:0] Off6
);

  assign Off6 = {{10{IR[5]}}, IR[5:0]};  // Bit_Extender bit_extender_1
endmodule

// Off9
module Offset9 (
  input  [15:0] IR,
  output [15:0] Off9
);

  assign Off9 = {{7{IR[8]}}, IR[8:0]};  // Bit_Extender bit_extender_1
endmodule

module Or16 (
  input  [15:0] in_1,
  output out_2
);

  wire [1:0] or_2_out;
  wire [7:0] or_1_out;

  assign or_1_out = in_1[7:0] | in_1[15:8];  // OR_Gate or_1, 8 bits wide
  assign or_2_out = or_1_out[1:0] | or_1_out[3:2] | or_1_out[5:4] | or_1_out[7:6];  // OR_Gate or_2, 2 bits wide
  or or_3 (out_2, or_2_out[0], or_2_out[1]);
endmodule

module RamCtrl (
  input  Exec,
  input  Fetch,
  input  Load,
  input  Store,
  output MemLoad,
  output MemStore
);

  wire and_1_out;

  and and_1 (and_1_out, Exec, Load);
  and and_2 (MemStore, Exec, Store);
  or or_1 (MemLoad, Fetch, and_1_out);
endmodule

module Registres (
  input  [2:0] SR1,
  input  [15:0] IN,
  input  [2:0] SR2,
  input  WriteReg,
  input  [2:0] DR_SR,
  output [15:0] R0,
  output [15:0] OUT_SR1,
  output [15:0] R1,
  output [15:0] R2,
  output [15:0] R3,
  output [15:0] OUT_SR2,
  output [15:0] R4,
  output [15:0] R5,
  output [15:0] OUT_SR,
  output [15:0] R6,
  output [15:0] R7
);

  wire decoder_1_out0, decoder_1_out1, decoder_1_out2, decoder_1_out3, decoder_1_out4, decoder_1_out5,
       decoder_1_out6, decoder_1_out7;

  Decoder #(.select(3), .disabled(0)) decoder_1 (
    .out0(decoder_1_out0), .out1(decoder_1_out1), .out2(decoder_1_out2), .out3(decoder_1_out3),
    .out4(decoder_1_out4), .out5(decoder_1_out5), .out6(decoder_1_out6), .out7(decoder_1_out7), .sel(DR_SR),
    .en(WriteReg));
  Register #(.width(16), .trigger("falling"), .Select("low")) u_R0 (
    .D(IN), .Q(R0), .clk(decoder_1_out0));  // open: en, clr
  Register #(.width(16), .trigger("falling"), .Select("low")) u_R1 (
    .D(IN), .Q(R1), .clk(decoder_1_out1));  // open: en, clr
  Register #(.width(16), .trigger("falling"), .Select("low")) u_R2 (
    .D(IN), .Q(R2), .clk(decoder_1_out2));  // open: en, clr
  Register #(.width(16), .trigger("falling"), .Select("low")) u_R3 (
    .D(IN), .Q(R3), .clk(decoder_1_out3));  // open: en, clr
  Register #(.width(16), .trigger("falling"), .Select("low")) u_R4 (
    .D(IN), .Q(R4), .clk(decoder_1_out4));  // open: en, clr
  Register #(.width(16), .trigger("falling"), .Select("low")) u_R5 (
    .D(IN), .Q(R5), .clk(decoder_1_out5));  // open: en, clr
  Register #(.width(16), .trigger("falling"), .Select("low")) u_R6 (
    .D(IN), .Q(R6), .clk(decoder_1_out6));  // open: en, clr
  Register #(.width(16), .trigger("falling"), .Select("low")) u_R7 (
    .D(IN), .Q(R7), .clk(decoder_1_out7));  // open: en, clr
  Multiplexer #(.select(3), .width(16), .enable("false")) multiplexer_1 (
    .in0(R0), .in1(R1), .in2(R2), .in3(R3), .in4(R4), .in5(R5), .in6(R6), .in7(R7), .out(OUT_SR1), .sel(SR1));
  Multiplexer #(.select(3), .width(16), .enable("false")) multiplexer_2 (
    .in0(R0), .in1(R1), .in2(R2), .in3(R3), .in4(R4), .in5(R5), .in6(R6), .in7(R7), .out(OUT_SR2), .sel(SR2));
  Multiplexer #(.select(3), .width(16), .enable("false")) multiplexer_3 (
    .in0(R0), .in1(R1), .in2(R2), .in3(R3), .in4(R4), .in5(R5), .in6(R6), .in7(R7), .out(OUT_SR), .sel(DR_SR));
endmodule

module RegPC (
  input  [15:0] IR,
  input  H,
  input  [15:0] R,
  input  Reset,
  input  Jump,
  input  TestNZP,
  output [15:0] PC,
  output Write_R7
);

  wire and_4_out, and_5_out, JMP, JSR, JSRR, or_2_out, or_3_out;
  wire [15:0] adder_1_out, adder_2_out, multiplexer_1_out, multiplexer_2_out, multiplexer_3_out,
       offset9_1_off9, offset11_1_sextoff11;

  and and_1 (JSR, ~IR[15], IR[14], ~IR[13], ~IR[12], IR[11]);  // AND_Gate
  and and_2 (JSRR, ~IR[15], IR[14], ~IR[13], ~IR[12], ~IR[11]);  // AND_Gate
  and and_3 (JMP, IR[15], IR[14], ~IR[13], ~IR[12]);  // AND_Gate
  Offset9 offset9_1 (.IR(IR), .Off9(offset9_1_off9));
  Offset11 offset11_1 (.IR(IR), .SEXTOff11(offset11_1_sextoff11));
  and and_4 (and_4_out, IR[14], Jump);
  and and_5 (and_5_out, Jump, TestNZP);
  Adder #(.width(16)) adder_1 (.a(PC), .b(16'h1), .out(adder_1_out));  // open: cin, cout
  Multiplexer #(.width(16), .disabled(0), .enable("false")) multiplexer_1 (
    .in0(offset9_1_off9), .in1(offset11_1_sextoff11), .out(multiplexer_1_out), .sel(and_4_out));
  or or_1 (Write_R7, JSR, JSRR);
  or or_2 (or_2_out, and_4_out, and_5_out);
  Adder #(.width(16)) adder_2 (.a(adder_1_out), .b(multiplexer_1_out), .out(adder_2_out));  // open: cin, cout
  Multiplexer #(.width(16), .disabled(0), .enable("false")) multiplexer_2 (
    .in0(adder_2_out), .in1(R), .out(multiplexer_2_out), .sel(or_3_out));
  or or_3 (or_3_out, JSRR, JMP);
  Multiplexer #(.width(16), .enable("false")) multiplexer_3 (
    .in0(adder_1_out), .in1(multiplexer_2_out), .out(multiplexer_3_out), .sel(or_2_out));
  Register #(.width(16), .trigger("falling"), .Select("low")) u_PC (
    .D(multiplexer_3_out), .Q(PC), .clk(H), .clr(Reset));  // open: en

  // Notes on the sheet:
  //   JSR ssi JMP et 14
  //   saut ssi JMP et (BR =>TestNZP)
  //   pour BR
  //   pour JSR
  //   PC <- PC + 1
  //   BaseR ssi JMP ou JSRR
  //   PC+Off
  //   BaseR
  //   Sauver R7 si JSR ou JSRR
  //   pas saut
  //   saut
endmodule

module Offset11 (
  input  [15:0] IR,
  output [15:0] SEXTOff11
);

  assign SEXTOff11 = {{5{IR[10]}}, IR[10:0]};  // Bit_Extender bit_extender_1
endmodule

module WriteVal (
  input  Load,
  input  [15:0] ALURes,
  input  [15:0] MemOUT,
  input  [15:0] IR,
  input  [15:0] PC,
  output [15:0] RegIN
);

  wire and_3_out, JSR, LEA, not_1_out;
  wire [1:0] multiplexer_1_out;
  wire [15:0] adder_1_out, offset9_1_off9;

  Offset9 offset9_1 (.IR(IR), .Off9(offset9_1_off9));
  and and_1 (LEA, ~IR[12], IR[13], IR[14], IR[15]);  // AND_Gate
  and and_2 (JSR, ~IR[12], ~IR[13], IR[14], ~IR[15]);  // AND_Gate
  Adder #(.width(16)) adder_1 (.a(offset9_1_off9), .b(PC), .out(adder_1_out));  // open: cin, cout
  not not_1 (not_1_out, LEA);
  and and_3 (and_3_out, not_1_out, Load);
  Multiplexer #(.width(2), .enable("false")) multiplexer_1 (
    .in0({JSR, LEA}), .in1({2{Load}}), .out(multiplexer_1_out), .sel(and_3_out));
  Multiplexer #(.select(2), .width(16), .enable("false")) multiplexer_2 (
    .in0(ALURes), .in1(adder_1_out), .in2(PC), .in3(MemOUT), .out(RegIN), .sel(multiplexer_1_out));

  // Notes on the sheet:
  //   A COMPLETER v2
  //   On ne peut pas avoir JSR et LEA en même temps$$On veut que LEA soit prioritaire sur LOAD $$On n'exécute donc LOAD que si LOAD = 1 et LEA = 0
  //   RegIN = $si JSR alors PC $sinon si LEA alors PC+SEXT(Offset9) $sinon si Load alors MemOUT $sinon ALURes  
  //   Si Load: code 11$Sinon code 01 ou 10
  //   10: JSR activé$01: LEA activé$11: Load activé$00: défaut
endmodule

module SCAN16 (
  input  [15:0] in_1,
  input  [15:0] in_2,
  output [15:0] out_3
);

  wire [15:1] and_1_out;

  assign {and_1_out, out_3[0]} = in_1 & in_2;  // AND_Gate and_1, 16 bits wide
  xor xor_1 (out_3[1], out_3[0], and_1_out[1]);
  xor xor_2 (out_3[2], out_3[1], and_1_out[2]);
  xor xor_3 (out_3[3], out_3[2], and_1_out[3]);
  xor xor_4 (out_3[4], out_3[3], and_1_out[4]);
  xor xor_5 (out_3[5], out_3[4], and_1_out[5]);
  xor xor_6 (out_3[6], out_3[5], and_1_out[6]);
  xor xor_7 (out_3[7], out_3[6], and_1_out[7]);
  xor xor_8 (out_3[8], out_3[7], and_1_out[8]);
  xor xor_9 (out_3[9], out_3[8], and_1_out[9]);
  xor xor_10 (out_3[10], out_3[9], and_1_out[10]);
  xor xor_11 (out_3[11], out_3[10], and_1_out[11]);
  xor xor_12 (out_3[12], out_3[11], and_1_out[12]);
  xor xor_13 (out_3[13], out_3[12], and_1_out[13]);
  xor xor_14 (out_3[14], out_3[13], and_1_out[14]);
  xor xor_15 (out_3[15], out_3[14], and_1_out[15]);
endmodule

module WriteR7 (
  input  Exec,
  input  [2:0] DR,
  input  WriteR7,
  input  WriteReg,
  input  [15:0] PC,
  input  [15:0] WriteValOut,
  output WriteReg_2,
  output [15:0] RegIn,
  output [2:0] DR_SR
);

  wire and_1_out;
  wire [15:0] adder_1_out;

  Adder #(.width(16)) adder_1 (.a(PC), .b(16'h1), .out(adder_1_out));  // open: cin, cout
  Multiplexer #(.width(16), .enable("false")) multiplexer_1 (
    .in0(WriteValOut), .in1(adder_1_out), .out(RegIn), .sel(WriteR7));
  or or_1 (WriteReg_2, WriteReg, and_1_out);
  and and_1 (and_1_out, Exec, WriteR7);
  Multiplexer #(.width(3), .enable("false")) multiplexer_2 (.in0(DR), .in1(3'b111), .out(DR_SR), .sel(WriteR7));
endmodule
